# Fritzing sketch OpenExhibits-Arduino-setup (saved by Fritzing 0.7.4b)
breadboards: 1

parts:
  U1 = Arduino Mega
  S1 = Round Pushbutton
  R1 = Rotary Potentiometer (Large) [maximum_resistance=100kΩ package=THT]
  R3 = Resistor [tolerance=±5% resistance=10k package="0603 [SMD]"]
  R4 = Resistor [tolerance=±5% resistance=10 package="0603 [SMD]"]
  LED2 = smd LED [color="Green (565nm)" package="0805 [SMD]"]
  RFID1 = RFID Reader
  LED3 = smd LED [color="Red (633nm)" package="0805 [SMD]"]

nets:
  GND: U1.GND, R1.leg1, R3.Pin_0, LED2.cathode, RFID1.GND, RFID1.+/-, LED3.cathode
  N1: U1.D2, S1.leg0, R3.Pin_1
  +5V: U1.+5V, R1.leg2, R4.Pin_1, RFID1.+5V
  N2: U1.A2, R1.wiper
  N3: U1.D50, RFID1.D0
  N4: U1.D52, LED2.anode, RFID1.RES
  N5: S1.leg1, R4.Pin_0
  N6: RFID1.LED, LED3.anode

notes:
  ID-12 wires:
  red +5V
  black gnd
  green Reset
  gray data (ttl)
  yellow buzzer/LED
  purple format select
